# Fritzing sketch lowerunit (saved by Fritzing 0.9.3b)
stripboards: 1

parts:
  U4 = Mystery Part - 12 pins [chip_label=? package=THT]
  J1 = female pin header, 6 pins [form="♀ (female)"]
  J2 = female pin header, 4 pins [form="♀ (female)"]
  J3 = female pin header, 6 pins [form="♀ (female)"]
  J4 = female pin header, 6 pins [form="♀ (female)"]
  J5 = female pin header, 4 pins [form="♀ (female)"]
  J6 = female pin header, 4 pins [form="♀ (female)"]
  U5 = Mystery Part - 8 pins [chip_label=? package=THT]

nets (from the breadboard view):
  N1: U4.pin1, J1.pin2, J2.pin2, J4.pin1, J5.pin3, U5.pin2
  N2: U4.pin2, J1.pin1, J2.pin1, J4.pin2, J5.pin4, U5.pin1
  N3: U4.pin3, J1.pin4, J4.pin3
  N4: U4.pin4, J4.pin4
  N5: U4.pin5, J4.pin5
  N6: U4.pin6, J4.pin6
  N7: U4.pin7, J3.pin6
  N8: U4.pin8, J3.pin5
  N9: U4.pin9, J3.pin4
  N10: U4.pin10, J1.pin3, J3.pin3
  N11: U4.pin11, J2.pin3, J3.pin2, J6.pin3, U5.pin7
  N12: U4.pin12, J2.pin4, J3.pin1, J6.pin4, U5.pin8
  N13: J5.pin1, U5.pin4
  N14: J5.pin2, U5.pin3
  N15: J6.pin1, U5.pin5
  N16: J6.pin2, U5.pin6

custom parts:
  Mystery Part - 12 pins: A dummy, proxy, ersatz, stand-in part for whatever you want. With 12 pins on a 100mil inline pin header footprint.
  Mystery Part - 8 pins: A dummy, proxy, ersatz, stand-in part for whatever you want. With 8 pins on a 200mil inline pin header footprint.
