# Fritzing sketch upperunit (saved by Fritzing 0.9.3b)
stripboards: 4

parts:
  Part1 = Arduino Leonardo (Rev3b)  # not connected
  J6 = male pin header, 4 pins [form="♂ (male)"]
  J7 = male pin header, 4 pins [form="♂ (male)"]
  J8 = male pin header, 4 pins [form="♂ (male)"]
  J11 = male pin header, 3 pins [form="♂ (male)"]
  J12 = male pin header, 3 pins [form="♂ (male)"]
  J13 = male pin header, 2 pins [form="♂ (male)"]
  J14 = male pin header, 2 pins [form="♂ (male)"]
  J10 = male pin header, 6 pins [form="♂ (male)"]
  J15 = male pin header, 1 pin [form="♂ (male)"]
  J16 = male pin header, 3 pins [form="♂ (male)"]
  J17 = male pin header, 2 pins [form="♂ (male)"]
  J19 = male pin header, 3 pins [form="♂ (male)"]
  J21 = male pin header, 6 pins [form="♂ (male)"]
  J23 = male pin header, 4 pins [form="♂ (male)"]
  J24 = male pin header, 4 pins [form="♂ (male)"]
  J25 = male pin header, 6 pins [form="♂ (male)"]
  J26 = male pin header, 1 pin [form="♂ (male)"]
  J27 = male pin header, 6 pins [form="♂ (male)"]
  J28 = male pin header, 2 pins [form="♂ (male)"]
  J29 = male pin header, 2 pins [form="♂ (male)"]
  J30 = male pin header, 3 pins [form="♂ (male)"]
  J31 = male pin header, 3 pins [form="♂ (male)"]
  J32 = male pin header, 4 pins [form="♂ (male)"]
  J33 = male pin header, 4 pins [form="♂ (male)"]
  J34 = male pin header, 4 pins [form="♂ (male)"]
  J22 = male pin header, 6 pins [form="♂ (male)"]
  J20 = male pin header, 7 pins [form="♂ (male)"]
  J35 = male pin header, 2 pins [form="♂ (male)"]
  J36 = male pin header, 3 pins [form="♂ (male)"]  # not connected
  J37 = male pin header, 4 pins [form="♂ (male)"]  # not connected
  J38 = male pin header, 2 pins [form="♂ (male)"]
  J39 = male pin header, 2 pins [form="♂ (male)"]
  J40 = male pin header, 2 pins [form="♂ (male)"]
  J41 = male pin header, 2 pins [form="♂ (male)"]
  J42 = male pin header, 2 pins [form="♂ (male)"]
  R8 = Resistor Mini [tolerance=±5% resistance=220 package=THT]
  R9 = Resistor Mini [tolerance=±5% resistance=220 package=THT]
  S1 = Momentary Switch [package=ksa_sealed_tac_switch]
  R10 = Vertical Resistor [tolerance=±5% resistance=220 package=THT]
  R11 = Vertical Resistor [tolerance=±5% resistance=220 package=THT]
  R12 = Vertical Resistor [tolerance=±5% resistance=220 package=THT]
  R13 = Vertical Resistor [tolerance=±5% resistance=220 package=THT]

nets:
  N1: J6.pin1, J6.pin2, J7.pin1, J7.pin2, J8.pin1, J8.pin4, J11.pin1, J11.pin2, J10.pin1
  N2: J6.pin3, J7.pin4, J14.pin1
  N3: J6.pin4, J7.pin3, J14.pin2
  N4: J8.pin2, J13.pin1
  N5: J8.pin3, J13.pin2
  N6: J11.pin3, J10.pin6
  N7: J12.pin1, J10.pin4
  N8: J12.pin2, J10.pin3
  N9: J10.pin5, J15.pin1
  N10: J16.pin1, J21.pin4
  N11: J16.pin2, J21.pin6
  N12: J16.pin3, J19.pin2, J21.pin3, J21.pin5, J23.pin1, J23.pin4, J24.pin1, J22.pin1, J22.pin2, J22.pin4, J20.pin2, J20.pin3, J20.pin4
  N13: J17.pin1, J24.pin3
  N14: J17.pin2, J24.pin4
  N15: J19.pin1, J21.pin1, J24.pin2
  N16: J23.pin2, J20.pin7
  N17: J23.pin3, J20.pin6
  N18: J25.pin1, S1.1, S1.2
  N19: J25.pin2, R8.Pin_1, R9.Pin_1
  N20: J25.pin3, R12.Pin_0, R13.Pin_0
  N21: J25.pin4, J25.pin5, R8.Pin_0, R9.Pin_0, R10.Pin_0, R10.Pin_1, R11.Pin_0, R11.Pin_1, R12.Pin_1, R13.Pin_1
  N22: J25.pin6, J35.pin1, J35.pin2, J39.pin1, J39.pin2, J41.pin1, J41.pin2
  N23: J26.pin1, J27.pin3, J31.pin3
  N24: J27.pin1, J31.pin1, J32.pin4, J33.pin4, J34.pin2
  N25: J27.pin4, J30.pin1
  N26: J27.pin5, J30.pin3
  N27: J27.pin6, J30.pin2
  N28: J28.pin1, J32.pin3
  N29: J28.pin2, J32.pin2
  N30: J29.pin1, J33.pin1, J34.pin3
  N31: J29.pin2, J33.pin2, J34.pin4
  N32: J31.pin2, J32.pin1, J33.pin3, J34.pin1
  N33: J22.pin3, J20.pin1
  N34: J22.pin5, J20.pin5
  N35: J38.pin1, J38.pin2, J40.pin1, J40.pin2, J42.pin1, J42.pin2
  N36: S1.3, S1.4

notes:
  // -- gnd, 5V, SCL,SDA -> OLED
  // -- 5V,gnd, SDA, SCL -> (lower module ADC_>FGM, OLED, TILT )
  // -- gnd, 7, 8, 5V -> GPS
  // --gnd, 13, 12, 11, 4, 3.3v-> SDCARD
  White, SDA
  Blue, SCL
  Black, Gnd
  Red, 5 V
  pink, 3.3 V
  LowerMod
  SDCARD
  OLED
  GPS
  GPS
  G,7,8,5V
  SDCARD
  G,3.3V,4,11,13,12,(g)
  OLED
  G,5V,SCL,SDA
  LowerMod
  5V,G,SDA,SCL
  3.3V
  5V
  G
  SCL
  SDA

custom parts:
  Resistor Mini: A generic resistor (0.25W)
  Vertical Resistor: A generic resistor (0.25W)
